# Fritzing sketch barrier (saved by Fritzing 0.9.3b)

parts:
  Часть1 = Arduino Pro Mini v13
  IC1 = Voltage Regulator LM1117 [package=sot223]
  Q2 = Basic FET P-Channel [package="TO220 [THT]"]
  R4 = Resistor [tolerance=±5% resistance=100k package=THT]
  Q3 = Basic FET P-Channel [package="TO220 [THT]"]
  R5 = Resistor [tolerance=±5% resistance=100k package=THT]
  Часть2 = Real Time Clock Module - DS1307 RTC Breakout Board

nets:
  N1: Часть1.RAW, IC1.OUT
  GND: Часть1.GND, IC1.ADJ, Часть2.GND
  VCC: Часть1.VCC, Часть2.5V
  N2: Часть1.D7, Q3.gate, R5.Pin_0
  N3: Часть1.D6_PWM, Q2.gate, R4.Pin_0

notes:
  a4
  a5
